// Logisim project Flip_Flop.circ as structural Verilog: 1 circuit, main circuit main
module main (
  input  in_1,
  input  in_2,
  output out_3,
  output out_4
);

  wire and_1_out, and_2_out;

  and and_1 (and_1_out, in_1, out_4);
  and and_2 (and_2_out, out_3, in_2);
  not not_1 (out_3, and_1_out);
  not not_2 (out_4, and_2_out);
endmodule
