// Logisim project Four-Bit_Adder.circ as structural Verilog: 3 circuits, main circuit main
module main (
  input  S1,
  input  R1,
  input  S2,
  input  R2,
  input  S3,
  input  R3,
  input  S4,
  input  R4,
  input  S5,
  input  R5,
  input  S6,
  input  R6,
  input  S7,
  input  R7,
  input  S8,
  input  R8,
  output O1,
  output O2,
  output O3,
  output O4,
  output Carry
);

  wire FA1_cout, FA1_sum, FA2_cout, FA2_sum, FA3_cout, FA3_sum, FA4_cout, FA4_sum, not_1_out, not_2_out,
       not_3_out, not_4_out, not_5_out, SRFFI1_x, SRFFI2_x, SRFFI3_x, SRFFI4_x, SRFFI5_x, SRFFI6_x, SRFFI7_x,
       SRFFI8_x;

  SR__Flip_Flop SRFFI1 (.S(S1), .R(R1), .X(SRFFI1_x));
  SR__Flip_Flop SRFFI2 (.S(S2), .R(R2), .X(SRFFI2_x));
  SR__Flip_Flop SRFFI3 (.S(S3), .R(R3), .X(SRFFI3_x));
  SR__Flip_Flop SRFFI4 (.S(S4), .R(R4), .X(SRFFI4_x));
  SR__Flip_Flop SRFFI5 (.S(S5), .R(R5), .X(SRFFI5_x));
  SR__Flip_Flop SRFFI6 (.S(S6), .R(R6), .X(SRFFI6_x));
  SR__Flip_Flop SRFFI7 (.S(S7), .R(R7), .X(SRFFI7_x));
  SR__Flip_Flop SRFFI8 (.S(S8), .R(R8), .X(SRFFI8_x));
  Full_Adder FA1 (.A(SRFFI1_x), .B(SRFFI2_x), .Cin(1'b0), .Sum(FA1_sum), .Cout(FA1_cout));
  Full_Adder FA2 (.A(SRFFI3_x), .B(SRFFI4_x), .Cin(FA1_cout), .Sum(FA2_sum), .Cout(FA2_cout));
  Full_Adder FA3 (.A(SRFFI5_x), .B(SRFFI6_x), .Cin(FA2_cout), .Sum(FA3_sum), .Cout(FA3_cout));
  Full_Adder FA4 (.A(SRFFI7_x), .B(SRFFI8_x), .Cin(FA3_cout), .Sum(FA4_sum), .Cout(FA4_cout));
  not not_1 (not_1_out, FA1_sum);
  not not_2 (not_2_out, FA2_sum);
  not not_3 (not_3_out, FA3_sum);
  not not_4 (not_4_out, FA4_sum);
  not not_5 (not_5_out, FA4_cout);
  SR__Flip_Flop SRFFO1 (.S(not_1_out), .R(FA1_sum), .X(O1));
  SR__Flip_Flop SRFFO2 (.S(not_2_out), .R(FA2_sum), .X(O2));
  SR__Flip_Flop SRFFO3 (.S(not_3_out), .R(FA3_sum), .X(O3));
  SR__Flip_Flop SRFFO4 (.S(not_4_out), .R(FA4_sum), .X(O4));
  SR__Flip_Flop SRFFO5 (.S(not_5_out), .R(FA4_cout), .X(Carry));
endmodule

module SR__Flip_Flop (
  input  S,
  input  R,
  output X
);

  wire nand_2_out;

  nand nand_1 (X, S, nand_2_out);
  nand nand_2 (nand_2_out, X, R);
endmodule

module Full_Adder (
  input  A,
  input  B,
  input  Cin,
  output Sum,
  output Cout
);

  wire and_1_out, and_2_out, xor_1_out;

  xor xor_1 (xor_1_out, A, B);
  and and_1 (and_1_out, A, B);
  xor xor_2 (Sum, xor_1_out, Cin);
  and and_2 (and_2_out, Cin, xor_1_out);
  or or_1 (Cout, and_2_out, and_1_out);
endmodule
