// Logisim project Full_Adder.circ as structural Verilog
module Full_Adder (
  input  A,
  input  B,
  input  C_in,
  output SUM,
  output C_out
);

  wire and_1_out, and_2_out, xor_1_out;

  xor xor_1 (xor_1_out, A, B);
  and and_1 (and_1_out, C_in, xor_1_out);
  and and_2 (and_2_out, A, B);
  xor xor_2 (SUM, xor_1_out, C_in);
  or or_1 (C_out, and_1_out, and_2_out);
endmodule
